# Fritzing sketch Circuit Diagram (saved by Fritzing 0.9.5d)
breadboards: 1

parts:
  Ultrasonic_Sensor(HC-SR04) = HC-SR04 Ultrasonic Distance Sensor
  DHT11_Temperature_and_Humidity_Sensor = DHT11 Humitidy and Temperature Sensor
  Water_Pump = water pump/motor  # not connected
  ESP32_Development_Board = ESP32S-HiLetgo [part_number=ESP32S-HiLetgo]
  Soil_Moisture_Sensor = FC-28 Soil Hygrometer Module - Probe
  HW-103_Comparator = CK-07 [package=THT]
  5V_Relay_Module = KY-019 5V Relay Module [package="Breakout board"]  # not connected
  LCD_Display_(I2C) = LCD1602-I2C
  Batteries = Battery  # not connected
  S1 = SPST Switch [package=r_sw_th]  # not connected
  S2 = SPST Switch [package=r_sw_th]  # not connected
  S3 = SPST Switch [package=r_sw_th]  # not connected
  S4 = SPST Switch [package=switch-spst-smd-a]  # not connected
  S5 = SPST Switch [package=r_sw_th]  # not connected
  S6 = SPST Switch [package=r_sw_th]  # not connected
  U1 = SWITCH-SPST-2 [package=r_sw_th]  # not connected
  S7 = SPST Switch [package=r_sw_th]  # not connected
  S9 = SPST Switch [package=switche-dpdt]  # not connected
  U2 = SWITCH-SPST-2 [package=r_sw_th]  # not connected
  U3 = SWITCH-SPST-2 [package=r_sw_th]  # not connected
  SG1 = Buzzer 12mm [package=buzzer-ccv-kit]  # not connected
  SG2 = Buzzer 12mm [package=buzzer-ccv-kit]  # not connected
  TMB12A05_Buzzer = Piezo Speaker

nets:
  N1: Ultrasonic_Sensor(HC-SR04).TRIG, ESP32_Development_Board.D13
  N2: Ultrasonic_Sensor(HC-SR04).ECHO, ESP32_Development_Board.D35
  N3: DHT11_Temperature_and_Humidity_Sensor.VDD, ESP32_Development_Board.EN
  N4: DHT11_Temperature_and_Humidity_Sensor.DATA, ESP32_Development_Board.D15
  GND: DHT11_Temperature_and_Humidity_Sensor.GND, ESP32_Development_Board.GND, ESP32_Development_Board.D23, LCD_Display_(I2C).GND
  N5: ESP32_Development_Board.D12, HW-103_Comparator.pin_1
  N6: ESP32_Development_Board.GPI012, LCD_Display_(I2C).VCC
  N7: ESP32_Development_Board.D5, TMB12A05_Buzzer.pin2
  N8: ESP32_Development_Board.D19, LCD_Display_(I2C).SDA
  N9: ESP32_Development_Board.RX0, LCD_Display_(I2C).SCL
  N10: Soil_Moisture_Sensor.POS, HW-103_Comparator.pin_5
  N11: Soil_Moisture_Sensor.NEG, HW-103_Comparator.pin_6

custom parts:
  DHT11 Humitidy and Temperature Sensor: DHT11 Humidity and Temperature Sensor
  water pump/motor: WATER PUMP BY ARDUBLOCKTR
  ESP32S-HiLetgo: HiLetgo ESP-WROOM-32 ESP32 ESP-32S Development Board 2.4GHz Dual-Mode WiFi + Bluetooth Dual Cores Microcontroller The ESP32 integrated with Antenna switches, RF Balun, power amplifiers, low-noise amplifiers, filters, and management modules, and the entire solution occupies the least area of PCB. 2.4 GHz Wi-Fi plus Bluetooth dual-mode chip, with TSMC Ultra-low power consumption 40nm technology,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
  FC-28 Soil Hygrometer Module - Probe: The FC-28 is a soil hygrometer module that uses the Texas Instruments LM393 comparator chip to provide an analog measurement of soil humidity.
  CK-07: Fc-51 Infrared Obstacle Avoidance Proximity Sensor module. IR transmitter led, receiver LED, lm393 compaitor and a pot. 3.3 V to 5V power.
  KY-019 5V Relay Module: KY-019 5V Relay module, used to control AC circuits. (Special thanks to vanepp for fixing the PCB holes and other errors)
  LCD1602-I2C: A standard character display, usually with 2x16 characters. Comes in many colors with LCM1602 IIC attached.
